# Fritzing sketch FT8_TX_Circuit (saved by Fritzing 1.0.6)
circuit board: 8.79862cm x 5.82513cm
breadboards: 1

parts:
  J1 = female pin header, 7 pins [form="♀ (female)"]
  J2 = female pin header, 15 pins [form="♀ (female)"]
  R1 = Resistor [tolerance=±5% resistance=10k power=0.25W package=THT]
  R2 = Resistor [tolerance=±5% resistance=10k power=0.25W package=THT]
  R3 = Resistor [tolerance=±5% resistance=1M power=0.25W package=THT]
  R4 = Resistor [tolerance=±5% resistance=4.7k power=0.25W package=THT]
  C1 = Ceramic Capacitor [capacitance=100nF voltage=35V package="100 mil [THT, multilayer]"]
  C2 = Ceramic Capacitor [capacitance=10nF voltage=35V package="100 mil [THT, multilayer]"]
  C3 = Ceramic Capacitor [capacitance=10nF voltage=35V package="100 mil [THT, multilayer]"]
  J3 = female pin header, 15 pins [form="♀ (female)"]
  J4 = female pin header, 2 pins [form="♀ (female)"]
  J5 = male pin header, 3 pins [form="♂ (male)"]
  J6 = male pin header, 3 pins [form="♂ (male)"]
  J7 = female pin header, 5 pins [form="♀ (female)"]  # not connected
  J9 = female pin header, 6 pins [form="♀ (female)"]
  J8 = female pin header, 6 pins [form="♀ (female)"]
  J10 = female pin header, 6 pins [form="♀ (female)"]

nets:
  N1: J1.pin4, J3.pin9
  N2: J1.pin5, J3.pin8
  N3: J1.pin6, J3.pin14, J4.pin2, J8.pin4
  N4: J1.pin7, J3.pin15, J4.pin1, J6.pin1, J8.pin3
  N5: J2.pin1, J8.pin6
  N6: J2.pin2, J8.pin5
  N7: J2.pin4, J2.pin9, R4.Pin_1, C2.0, C3.0, J5.pin3, J6.pin2
  N8: J2.pin7, J6.pin3
  N9: J2.pin10, R2.Pin_1, C3.1
  N10: R1.Pin_0, R3.Pin_1, R4.Pin_0, C1.0
  N11: R1.Pin_1, R2.Pin_0, C2.1
  N12: R3.Pin_0, J3.pin2
  N13: C1.1, J5.pin1, J5.pin2
  N14: J9.pin1, J10.pin1
  N15: J9.pin2, J10.pin2
  N16: J9.pin3, J10.pin3
  N17: J9.pin4, J10.pin4
  N18: J9.pin5, J10.pin5
  N19: J9.pin6, J10.pin6

notes:
  3.3V
  Arduino Nano
  Si5351
  SDA / A4
  SCL / A5
  FT8 In / D7
  Gnd
  Gnd / D6
  5V
  From PC
  Relais
  Relais / D4
  DL1SKD
  FT8 FTX Module
  V0.1
  Nano
  RX
  TX
  S
  R
  L
  Pwr
