# Fritzing sketch LPF (saved by Fritzing 1.0.6)
circuit board: 5.49697cm x 1.82984cm
breadboards: 1

parts:
  L2 = Inductor [inductance=1.7µH package="400 mil [THT]"]
  C1 = Ceramic Capacitor [capacitance=270pF voltage=35V package="100 mil [THT, multilayer]"]
  C2 = Ceramic Capacitor [capacitance=680pF voltage=35V package="100 mil [THT, multilayer]"]
  C3 = Ceramic Capacitor [capacitance=680pF voltage=35V package="100 mil [THT, multilayer]"]
  C4 = Ceramic Capacitor [capacitance=270pF voltage=35V package="100 mil [THT, multilayer]"]
  J1 = male pin header, 2 pins [form="♂ (male)"]
  J2 = male pin header, 2 pins [form="♂ (male)"]
  J3 = male pin header, 2 pins [form="♂ (male)"]
  J4 = male pin header, 2 pins [form="♂ (male)"]
  L1 = Inductor [inductance=1.4µH package="400 mil [THT]"]
  L3 = Inductor [inductance=1.4µH package="400 mil [THT]"]

nets:
  N1: L2.pin_0, C3.1, L3.pin_1
  N2: L2.pin_1, C2.1, L1.pin_0
  N3: C1.0, C2.0, C3.0, C4.0, J2.pin1, J2.pin2, J4.pin1, J4.pin2
  N4: C1.1, J1.pin1, J1.pin2, L1.pin_1
  N5: C4.1, J3.pin1, J3.pin2, L3.pin_0
