# Fritzing sketch TX (saved by Fritzing 1.0.6)
circuit board: 7.2cm x 4.9cm
breadboards: 1

parts:
  U1 = Arduino Nano (Rev3.0) (ICSP)
  C1 = Ceramic Capacitor [capacitance=100nF voltage=35V package="100 mil [THT, multilayer]"]
  R1 = Resistor [tolerance=±5% power=0.25W resistance=1M package=THT]
  R2 = Resistor [tolerance=±5% power=0.25W resistance=4.7k package=THT]
  R3 = Resistor [tolerance=±5% power=0.25W resistance=10k package=THT]
  R4 = Resistor [tolerance=±5% power=0.25W resistance=10k package=THT]
  C2 = Ceramic Capacitor [capacitance=100nF voltage=35V package="100 mil [THT, multilayer]"]
  C3 = Ceramic Capacitor [capacitance=100nF voltage=35V package="100 mil [THT, multilayer]"]
  TX_Relais = male pin header, 3 pins [form="♂ (male)"]
  UART_Com = male pin header, 3 pins [form="♂ (male)"]
  VCC = female pin header, 2 pins [form="♀ (female)"]
  U2 = Adafruit Si5351A Clock Generator [part_number="Adafruit #2045"]
  Mic = male pin header, 2 pins [form="♂ (male)"]
  LED_Out = male pin header, 3 pins [form="♂ (male)"]

nets:
  N1: U1.D1/TX, UART_Com.pin1
  N2: U1.D0/RX, UART_Com.pin2
  GND: U1.GND, U1.D6, R2.Pin_1, C2.0, C3.0, TX_Relais.pin1, UART_Com.pin3, VCC.pin2, U2.GND, Mic.pin2, LED_Out.pin3
  N3: U1.D4, TX_Relais.pin2
  N4: U1.D5, LED_Out.pin2
  N5: U1.D7, R4.Pin_1, C3.1
  N6: U1.D9, LED_Out.pin1
  N7: U1.VIN, VCC.pin1
  5V: U1.5V, TX_Relais.pin3, U2.VIN
  N8: U1.A5, U2.SCL
  N9: U1.A4, U2.SDA
  N10: U1.3V3, R1.Pin_0
  N11: C1.0, R1.Pin_1, R2.Pin_0, R3.Pin_0
  N12: C1.1, Mic.pin1
  N13: R3.Pin_1, R4.Pin_0, C2.1

notes:
  DL1SKD
  ATS-FT8-TX V0.1
  - O +
  - RX TX
  + -

custom parts:
  Adafruit Si5351A Clock Generator: Never hunt around for another crystal again, with the Si5351A clock generator breakout from Adafruit! This chip has a precision 25MHz crystal reference and internal PLL and dividers so it can generate just about any frequency, from <8KHz up to 150+ MHz. The Si5351A clock generator is an I2C controller clock generator. It uses the onboard precision clock to drive multiple PLL's and clock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
